// Logisim project adder_sub_OV.circ as structural Verilog: 4 circuits, main circuit fa
module fa (
  input  A,
  input  B,
  input  Cin,
  output Sum,
  output Cout
);

  wire and_1_out, and_2_out, and_3_out;

  and and_1 (and_1_out, Cin, B);
  and and_2 (and_2_out, Cin, A);
  and and_3 (and_3_out, B, A);
  xor xor_1 (Sum, Cin, B, A);
  or or_1 (Cout, and_1_out, and_2_out, and_3_out);
endmodule

module _4b_ripple_carry (
  input  [3:0] A,
  input  [3:0] B,
  input  Cin,
  output Cout,
  output [3:0] Sum
);

  wire fa_2_cout, fa_3_cout, fa_4_cout;

  fa fa_1 (.Sum(Sum[3]), .Cout(Cout), .A(A[3]), .B(B[3]), .Cin(fa_2_cout));
  fa fa_2 (.Sum(Sum[2]), .Cout(fa_2_cout), .A(A[2]), .B(B[2]), .Cin(fa_3_cout));
  fa fa_3 (.Sum(Sum[1]), .Cout(fa_3_cout), .A(A[1]), .B(B[1]), .Cin(fa_4_cout));
  fa fa_4 (.Sum(Sum[0]), .Cout(fa_4_cout), .A(A[0]), .B(B[0]), .Cin(Cin));
endmodule

module add_sub_ov_v2 (
  input  [3:0] A,
  input  [3:0] B,
  input  add_n_sub,
  output OV,
  output Cout,
  output [3:0] Sum
);

  wire xor_2_out, xor_3_out, xor_4_out;
  wire [3:0] bit_extender_1_out, xor_1_out;

  _4b_ripple_carry u_4b_ripple_carry_1 (.A(A), .B(xor_1_out), .Cin(add_n_sub), .Cout(Cout), .Sum(Sum));
  assign xor_1_out = B ^ bit_extender_1_out;  // XOR_Gate xor_1, 4 bits wide
  assign bit_extender_1_out = {{3{add_n_sub}}, add_n_sub};  // Bit_Extender bit_extender_1
  xor xor_2 (xor_2_out, B[3], A[3]);
  xor xor_3 (xor_3_out, Sum[3], Cout);
  xor xor_4 (xor_4_out, xor_2_out, add_n_sub);
  xor xor_5 (OV, xor_4_out, xor_3_out);
endmodule

module add_sub_ov (
  input  [3:0] A,
  input  [3:0] B,
  input  add_n_sub,
  output OV,
  output Cout,
  output [3:0] Sum
);

  wire xnor_1_out, xor_2_out, xor_3_out;
  wire [3:0] bit_extender_1_out, xor_1_out;

  _4b_ripple_carry u_4b_ripple_carry_1 (.A(A), .B(xor_1_out), .Cin(add_n_sub), .Cout(Cout), .Sum(Sum));
  assign xor_1_out = B ^ bit_extender_1_out;  // XOR_Gate xor_1, 4 bits wide
  assign bit_extender_1_out = {{3{add_n_sub}}, add_n_sub};  // Bit_Extender bit_extender_1
  xor xor_2 (xor_2_out, Sum[3], Cout);
  xnor xnor_1 (xnor_1_out, B[3], A[3]);
  xor xor_3 (xor_3_out, xnor_1_out, add_n_sub);
  and and_1 (OV, xor_3_out, xor_2_out);

  // Notes on the sheet:
  //   Same sign?
  //   Cout == Sum sign?
  //   opposite condition when sub
endmodule
