// Logisim project 1b_adder.circ as structural Verilog: 2 circuits, main circuit 1b_adder
module _1b_adder (
  input  cin,
  input  a,
  input  b,
  output cout,
  output s
);

  wire and_1_out, and_2_out, or_1_out;

  xor xor_1 (s, b, a, cin);
  and and_1 (and_1_out, b, a);
  or or_1 (or_1_out, b, a);
  and and_2 (and_2_out, or_1_out, cin);
  or or_2 (cout, and_1_out, and_2_out);
endmodule

module _2b_adder (
  input  b1,
  input  a1,
  input  b0,
  input  a0,
  input  cin,
  output cout,
  output s1,
  output s0
);

  wire n1b_adder_2_cout;

  _1b_adder u_1b_adder_1 (.cin(n1b_adder_2_cout), .a(b1), .b(a1), .cout(cout), .s(s1));
  _1b_adder u_1b_adder_2 (.cin(cin), .a(b0), .b(a0), .cout(n1b_adder_2_cout), .s(s0));
endmodule
