// Logisim project sequential_multiplier.circ as structural Verilog: 1 circuit, main circuit seq_mult
module seq_mult (
  input  [7:0] Multiplicand,
  input  [7:0] Multiplier,
  input  init,
  input  load,
  input  clk,
  input  rst
);

  wire adder_1_cout, d_ff_1_q, shift_register_1_out;
  wire [7:0] adder_1_out, multiplexer_1_out, multiplexer_2_out, shift_register_1_q7, shift_register_1_q15;

  Multiplexer #(.width(8), .enable("false")) multiplexer_1 (
    .in0({8{1'b0}}), .in1(Multiplicand), .out(multiplexer_1_out), .sel(d_ff_1_q));
  Adder adder_1 (.a(multiplexer_1_out), .b(shift_register_1_q7), .out(adder_1_out), .cout(adder_1_cout));  // open: cin
  Counter counter_1 (.clk(load), .clr(rst));  // open: load, D, count, Q, carry
  Shift_Register #(.length(16)) shift_register_1 (
    .in(adder_1_cout), .clk(clk), .out(shift_register_1_out), .load(load), .clr(rst), .d0(adder_1_out[7]),
    .q0(shift_register_1_q7[7]), .d1(adder_1_out[6]), .q1(shift_register_1_q7[6]), .d2(adder_1_out[5]),
    .q2(shift_register_1_q7[5]), .d3(adder_1_out[4]), .q3(shift_register_1_q7[4]), .d4(adder_1_out[3]),
    .q4(shift_register_1_q7[3]), .d5(adder_1_out[2]), .q5(shift_register_1_q7[2]), .d6(adder_1_out[1]),
    .q6(shift_register_1_q7[1]), .d7(adder_1_out[0]), .q7(shift_register_1_q7[0]), .d8(multiplexer_2_out[7]),
    .q8(shift_register_1_q15[7]), .d9(multiplexer_2_out[6]), .q9(shift_register_1_q15[6]),
    .d10(multiplexer_2_out[5]), .q10(shift_register_1_q15[5]), .d11(multiplexer_2_out[4]),
    .q11(shift_register_1_q15[4]), .d12(multiplexer_2_out[3]), .q12(shift_register_1_q15[3]),
    .d13(multiplexer_2_out[2]), .q13(shift_register_1_q15[2]), .d14(multiplexer_2_out[1]),
    .q14(shift_register_1_q15[1]), .d15(multiplexer_2_out[0]), .q15(shift_register_1_q15[0]));  // open: shift
  Multiplexer #(.width(8), .enable("false")) multiplexer_2 (
    .in0(shift_register_1_q15), .in1(Multiplier), .out(multiplexer_2_out), .sel(init));
  D_Flip_Flop d_ff_1 (.clk(clk), .D(shift_register_1_out), .Q(d_ff_1_q), .reset(rst));  // open: Qn, preset, en

  // Notes on the sheet:
  //   Instructions
  //   1.- Enter multiplicand and multiplier
  //   2.- Set init and load to 1. Clock pulse once
  //   3.- Clear init and load to 0. Clock pulse once
  //   4.- Set load to 1. Clock pulse once
  //   5.- Clear load to 0. Clock pulse once
  //   6.- Repeat steps 4 and 5 8 times
endmodule
